# Fritzing sketch attiny-dht (saved by Fritzing 0.9.3b)
breadboards: 1

parts:
  R1 = Resistor [tolerance=±5% resistance=220 package=THT]
  U2 = attiny85 [package=dip]
  RHT1 = Humidity and Temperature Sensor RHT03
  VCC1 = 4 x AAA Battery Mount
  U3 = FS1000A - 433Mhz RF Transmitter [package=THT]

nets:
  VCC: R1.Pin_0, U2.Pin_8, RHT1.Vcc, VCC1.+, U3.VCC
  N1: R1.Pin_1, U2.Pin_3, RHT1.Data-signal
  N2: U2.Pin_4, RHT1.GND_2, VCC1.-, U3.GND
  N3: U2.Pin_7, U3.DATA

custom parts:
  FS1000A - 433Mhz RF Transmitter: This is 433Mhz RF transmitter with receiver kit for Arduino ARM MCU wireless Application environment: Remote control switch, receiver module, motorcycles, automobile anti-theft products, home security products, electric doors, shutter doors, windows, remote control socket, remote control LED, remote audio remote control electric doors, garage door remote control, remote control retractable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
